// Logisim project ForwardingLogic.circ as structural Verilog: 2 circuits, main circuit main
module Forwarding (
  input  [2:0] Rs,
  input  EX_RegWr,
  input  Mem_RegWr,
  input  WB_RegWr,
  input  [2:0] Rd2,
  input  [2:0] Rd3,
  input  [2:0] Rd4,
  input  [2:0] Rt
);

  wire AS0_out, AS1_out, BS0_out, BS1_out, comparator_1_eq, comparator_2_eq, comparator_3_eq,
       comparator_4_eq, comparator_5_eq, comparator_6_eq, not_1_out, not_2_out, not_3_out, not_4_out,
       or_1_out, or_2_out, or_3_out, or_4_out, Zero_2_out, Zero_out, ZGC_2_out, ZGC_out, ZXA_2_out, ZXA_out,
       ZYB_2_out, ZYB_out;

  and ZGC (ZGC_out, comparator_3_eq, WB_RegWr, Zero_out);
  Comparator #(.width(3), .mode("unsigned")) comparator_1 (.a(Rt), .b(Rd2), .eq(comparator_1_eq));  // open: gt, lt
  and ZYB (ZYB_out, Mem_RegWr, comparator_2_eq, Zero_out);
  or or_1 (or_1_out, ZGC_out, ZYB_out);
  and AS1 (AS1_out, or_1_out, not_1_out);
  // Probe on AS1_out
  Comparator #(.width(3), .mode("unsigned")) comparator_2 (.a(Rt), .b(Rd3), .eq(comparator_2_eq));  // open: gt, lt
  not not_1 (not_1_out, ZXA_out);
  not not_2 (not_2_out, ZYB_out);
  or Zero (Zero_out, Rt[2], Rt[1], Rt[0]);
  Comparator #(.width(3), .mode("unsigned")) comparator_3 (.a(Rt), .b(Rd4), .eq(comparator_3_eq));  // open: gt, lt
  and ZXA (ZXA_out, comparator_1_eq, EX_RegWr, Zero_out);
  or or_2 (or_2_out, ZGC_out, ZXA_out);
  and AS0 (AS0_out, or_2_out, not_2_out);
  // Probe on AS0_out
  and ZGC_2 (ZGC_2_out, comparator_6_eq, WB_RegWr, Zero_2_out);
  Comparator #(.width(3), .mode("unsigned")) comparator_4 (.a(Rd2), .b(Rs), .eq(comparator_4_eq));  // open: gt, lt
  or or_3 (or_3_out, ZGC_2_out, ZYB_2_out);
  Comparator #(.width(3), .mode("unsigned")) comparator_5 (.a(Rd3), .b(Rs), .eq(comparator_5_eq));  // open: gt, lt
  and ZYB_2 (ZYB_2_out, comparator_5_eq, Mem_RegWr, Zero_2_out);
  not not_3 (not_3_out, ZYB_2_out);
  and BS1 (BS1_out, or_3_out, not_4_out);
  // Probe on BS1_out
  Comparator #(.width(3), .mode("unsigned")) comparator_6 (.a(Rd4), .b(Rs), .eq(comparator_6_eq));  // open: gt, lt
  and ZXA_2 (ZXA_2_out, comparator_4_eq, EX_RegWr, Zero_2_out);
  not not_4 (not_4_out, ZXA_2_out);
  or or_4 (or_4_out, ZGC_2_out, ZXA_2_out);
  and BS0 (BS0_out, or_4_out, not_3_out);
  // Probe on BS0_out
  or Zero_2 (Zero_2_out, Rs[2], Rs[1], Rs[0]);

  // Notes on the sheet:
  //   Rs=Rd2
  //   Rs=Rd3
  //   Rs=Rd4
  //   Rs=Rd2
  //   Rs=Rd3
  //   Rs=Rd4
endmodule

// Forwarding
module main (
  input  [2:0] Rs,
  input  EX_RegWr,
  input  Mem_RegWr,
  input  WB_RegWr,
  input  [2:0] Rd2,
  input  [2:0] Rd3,
  input  [2:0] Rd4,
  input  [2:0] Rt
);

  wire AS0_out, AS1_out, BS0_out, BS1_out, comparator_1_eq, comparator_2_eq, comparator_3_eq,
       comparator_4_eq, comparator_5_eq, comparator_6_eq, not_1_out, not_2_out, not_3_out, not_4_out,
       or_1_out, or_2_out, or_3_out, or_4_out, Zero_2_out, Zero_out, ZGC_2_out, ZGC_out, ZXA_2_out, ZXA_out,
       ZYB_2_out, ZYB_out;

  and ZGC (ZGC_out, comparator_3_eq, WB_RegWr, Zero_out);
  Comparator #(.width(3), .mode("unsigned")) comparator_1 (.a(Rt), .b(Rd2), .eq(comparator_1_eq));  // open: gt, lt
  and ZYB (ZYB_out, Mem_RegWr, comparator_2_eq, Zero_out);
  or or_1 (or_1_out, ZGC_out, ZYB_out);
  and AS1 (AS1_out, or_1_out, not_1_out);
  // Probe on AS1_out
  Comparator #(.width(3), .mode("unsigned")) comparator_2 (.a(Rt), .b(Rd3), .eq(comparator_2_eq));  // open: gt, lt
  not not_1 (not_1_out, ZXA_out);
  not not_2 (not_2_out, ZYB_out);
  or Zero (Zero_out, Rt[2], Rt[1], Rt[0]);
  Comparator #(.width(3), .mode("unsigned")) comparator_3 (.a(Rt), .b(Rd4), .eq(comparator_3_eq));  // open: gt, lt
  and ZXA (ZXA_out, comparator_1_eq, EX_RegWr, Zero_out);
  or or_2 (or_2_out, ZGC_out, ZXA_out);
  and AS0 (AS0_out, or_2_out, not_2_out);
  // Probe on AS0_out
  and ZGC_2 (ZGC_2_out, comparator_6_eq, WB_RegWr, Zero_2_out);
  Comparator #(.width(3), .mode("unsigned")) comparator_4 (.a(Rd2), .b(Rs), .eq(comparator_4_eq));  // open: gt, lt
  or or_3 (or_3_out, ZGC_2_out, ZYB_2_out);
  Comparator #(.width(3), .mode("unsigned")) comparator_5 (.a(Rd3), .b(Rs), .eq(comparator_5_eq));  // open: gt, lt
  and ZYB_2 (ZYB_2_out, comparator_5_eq, Mem_RegWr, Zero_2_out);
  not not_3 (not_3_out, ZYB_2_out);
  and BS1 (BS1_out, or_3_out, not_4_out);
  // Probe on BS1_out
  Comparator #(.width(3), .mode("unsigned")) comparator_6 (.a(Rd4), .b(Rs), .eq(comparator_6_eq));  // open: gt, lt
  and ZXA_2 (ZXA_2_out, comparator_4_eq, EX_RegWr, Zero_2_out);
  not not_4 (not_4_out, ZXA_2_out);
  or or_4 (or_4_out, ZGC_2_out, ZXA_2_out);
  and BS0 (BS0_out, or_4_out, not_3_out);
  // Probe on BS0_out
  or Zero_2 (Zero_2_out, Rs[2], Rs[1], Rs[0]);

  // Notes on the sheet:
  //   Rs=Rd2
  //   Rs=Rd3
  //   Rs=Rd4
  //   Rs=Rd2
  //   Rs=Rd3
  //   Rs=Rd4
endmodule
