// Logisim project Full Circuit.circ as structural Verilog: 4 circuits, main circuit main
module main (
  input  [23:0] Data_A
);

  wire [23:0] rom_1_data;

  ROM #(.addrWidth(24), .dataWidth(24)) rom_1 (.addr(Data_A), .data(rom_1_data));  // open: sel
  // Probe on {rom_1_data[7], rom_1_data[8], rom_1_data[9]}
  // Probe on {rom_1_data[10], rom_1_data[11], rom_1_data[12]}
  // Probe on {rom_1_data[13], rom_1_data[14], rom_1_data[15]}

  // Notes on the sheet:
  //   contents of rom_1 (hex, n*v repeats v):
  //   b970 11 11
endmodule

// Forwarding
module Forwarding_Logic (
  input  [2:0] Rs,
  input  EX_RegWr,
  input  Mem_RegWr,
  input  WB_RegWr,
  input  [2:0] Rd2,
  input  [2:0] Rd3,
  input  [2:0] Rd4,
  input  [2:0] Rt,
  output [1:0] SB,
  output [1:0] SA
);

  wire comparator_1_eq, comparator_2_eq, comparator_3_eq, comparator_4_eq, comparator_5_eq, comparator_6_eq,
       not_1_out, not_2_out, not_3_out, not_4_out, or_1_out, or_2_out, or_3_out, or_4_out, Zero_2_out,
       Zero_out, ZGC_2_out, ZGC_out, ZXA_2_out, ZXA_out, ZYB_2_out, ZYB_out;

  and ZGC (ZGC_out, comparator_3_eq, WB_RegWr, Zero_out);
  Comparator #(.width(3), .mode("unsigned")) comparator_1 (.a(Rt), .b(Rd2), .eq(comparator_1_eq));  // open: gt, lt
  and ZYB (ZYB_out, Mem_RegWr, comparator_2_eq, Zero_out);
  or or_1 (or_1_out, ZGC_out, ZYB_out);
  and AS1 (SA[1], or_1_out, not_2_out);
  Comparator #(.width(3), .mode("unsigned")) comparator_2 (.a(Rt), .b(Rd3), .eq(comparator_2_eq));  // open: gt, lt
  not not_1 (not_1_out, ZYB_out);
  not not_2 (not_2_out, ZXA_out);
  or Zero (Zero_out, Rt[2], Rt[1], Rt[0]);
  Comparator #(.width(3), .mode("unsigned")) comparator_3 (.a(Rt), .b(Rd4), .eq(comparator_3_eq));  // open: gt, lt
  and ZXA (ZXA_out, comparator_1_eq, EX_RegWr, Zero_out);
  or or_2 (or_2_out, ZGC_out, ZXA_out);
  and AS0 (SA[0], or_2_out, not_1_out);
  and ZGC_2 (ZGC_2_out, comparator_6_eq, WB_RegWr, Zero_2_out);
  Comparator #(.width(3), .mode("unsigned")) comparator_4 (.a(Rd2), .b(Rs), .eq(comparator_4_eq));  // open: gt, lt
  or or_3 (or_3_out, ZGC_2_out, ZYB_2_out);
  Comparator #(.width(3), .mode("unsigned")) comparator_5 (.a(Rd3), .b(Rs), .eq(comparator_5_eq));  // open: gt, lt
  and ZYB_2 (ZYB_2_out, comparator_5_eq, Mem_RegWr, Zero_2_out);
  not not_3 (not_3_out, ZYB_2_out);
  and BS1 (SB[1], or_3_out, not_4_out);
  Comparator #(.width(3), .mode("unsigned")) comparator_6 (.a(Rd4), .b(Rs), .eq(comparator_6_eq));  // open: gt, lt
  and ZXA_2 (ZXA_2_out, comparator_4_eq, EX_RegWr, Zero_2_out);
  not not_4 (not_4_out, ZXA_2_out);
  or or_4 (or_4_out, ZGC_2_out, ZXA_2_out);
  and BS0 (SB[0], or_4_out, not_3_out);
  or Zero_2 (Zero_2_out, Rs[2], Rs[1], Rs[0]);

  // Notes on the sheet:
  //   Rs=Rd2
  //   Rs=Rd3
  //   Rs=Rd4
  //   Rs=Rd2
  //   Rs=Rd3
  //   Rs=Rd4
endmodule

// Rt
module Full_Circuit (
  input  PC_Clear_for_testing
);

  wire alu_1_p3, clock_1_out, comparator_1_eq, M0_out, main_1_p2, main_1_p5, main_1_p6, not_1_out, or_1_out,
       or_2_out, WB_q;
  wire [1:0] forwarding_logic_1_sa, forwarding_logic_1_sb, main_1_p4, undriven;
  wire [2:0] main_1_p8, multiplexer_3_out, Rd2_q, Rd3_q, Rd4_q;
  wire [3:0] MEM_q;
  wire [5:0] main_1_p7;
  wire [8:8] main_1_p9;
  wire [9:0] EX_q, multiplexer_7_out;
  wire [16:0] register_1_q_2;
  wire [23:0] adder_1_out, adder_2_out, adder_3_out, alu_1_p5, Alu_Res_q, bit_extender_1_out,
       bit_extender_2_out, bit_extender_3_out, bit_extender_4_out, BTA_q, DataA_q, DataB_q, Immediate_q,
       Jump_q, multiplexer_1_out, multiplexer_2_out, multiplexer_4_out, multiplexer_5_out, multiplexer_6_out,
       multiplexer_8_out, multiplexer_9_out, NPC_q, Program_Counter_q, ram_1_data, RB_q, register_2_q,
       register_file_1_data_a, register_file_1_data_b, register_file_1_r0, register_file_1_r1,
       register_file_1_r2, register_file_1_r3, register_file_1_r4, register_file_1_r5, register_file_1_r6,
       register_file_1_r7, rom_1_data;
  wire [23:17] register_1_q;

  Multiplexer #(.select(2), .width(24)) multiplexer_1 (
    .in0(adder_1_out), .in1(Jump_q), .in2(register_file_1_data_a), .in3(BTA_q), .out(multiplexer_1_out),
    .sel(main_1_p4));  // open: en
  assign bit_extender_1_out = {{23{1'b0}}, 1'b1};  // Bit_Extender bit_extender_1
  Clock #(.highDuration(60), .lowDuration(60)) clock_1 (.out(clock_1_out));
  Adder #(.width(24)) adder_1 (
    .a(Program_Counter_q), .b(bit_extender_1_out), .out(adder_1_out), .cin(1'b0));  // open: cout
  Register #(.width(24)) NPC (.D(adder_1_out), .en(1'b1), .Q(NPC_q), .clk(clock_1_out), .clr(1'b0));
  Register #(.width(24)) Program_Counter (
    .D(multiplexer_1_out), .en(not_1_out), .Q(Program_Counter_q), .clk(clock_1_out),
    .clr(PC_Clear_for_testing));
  ROM #(.addrWidth(24), .dataWidth(24)) rom_1 (.addr(Program_Counter_q), .data(rom_1_data), .sel(1'b1));
  Multiplexer #(.width(24)) multiplexer_2 (
    .in0(rom_1_data), .in1({24{1'b0}}), .out(multiplexer_2_out), .sel(main_1_p6));  // open: en
  Register #(.width(24)) register_1 (
    .D(multiplexer_2_out), .en(not_1_out), .Q({register_1_q, register_1_q_2}), .clk(clock_1_out));  // open: clr
  not not_1 (not_1_out, M0_out);
  // CU_1__main main_1: pin names not known; wires that end beside it: EX_q[9], main_1_p2, {register_1_q, register_1_q_2[16]}, main_1_p4, main_1_p5, main_1_p6, main_1_p7, main_1_p8, main_1_p9[8]
  and M0 (M0_out, EX_q[5], or_1_out);
  or or_1 (or_1_out, forwarding_logic_1_sb[1], forwarding_logic_1_sb[0], forwarding_logic_1_sa[1], forwarding_logic_1_sa[0]);
  or or_2 (or_2_out, main_1_p5, M0_out);
  Adder #(.width(24)) adder_2 (.a(bit_extender_4_out), .b(NPC_q), .out(adder_2_out), .cin(1'b0));  // open: cout
  Forwarding_Logic forwarding_logic_1 (
    .EX_RegWr(EX_q[7]), .Mem_RegWr(MEM_q[3]), .WB_RegWr(WB_q), .Rd2(Rd2_q), .Rd3(Rd3_q), .Rd4(Rd4_q),
    .Rt(register_1_q_2[9:7]), .Rs(register_1_q_2[12:10]), .SA(forwarding_logic_1_sa),
    .SB(forwarding_logic_1_sb));
  assign bit_extender_2_out = {{14{1'b0}}, register_1_q_2[9:0]};  // Bit_Extender bit_extender_2
  assign bit_extender_3_out = {{14{register_1_q_2[9]}}, register_1_q_2[9:0]};  // Bit_Extender bit_extender_3
  assign bit_extender_4_out = {{7{1'b0}}, register_1_q_2};  // Bit_Extender bit_extender_4
  Register_File register_file_1 (
    .RA(register_1_q_2[9:7]), .RB(register_1_q_2[12:10]), .Data_A(register_file_1_data_a),
    .Data_B(register_file_1_data_b), .RW(Rd4_q), .CLK(clock_1_out), .RegRW(WB_q), .BusWR(register_2_q),
    .R0(register_file_1_r0), .R1(register_file_1_r1), .R2(register_file_1_r2), .R3(register_file_1_r3),
    .R4(register_file_1_r4), .R5(register_file_1_r5), .R6(register_file_1_r6), .R7(register_file_1_r7));
  Multiplexer #(.select(2), .width(3)) multiplexer_3 (
    .in0(register_1_q_2[15:13]), .in1(3'b001), .in2(3'b111), .out(multiplexer_3_out), .sel(undriven));  // open: in3, en
  Adder #(.width(24)) adder_3 (.a(NPC_q), .b(bit_extender_2_out), .out(adder_3_out), .cin(1'b0));  // open: cout
  Multiplexer #(.width(24)) multiplexer_4 (
    .in0(bit_extender_3_out), .in1(bit_extender_4_out), .out(multiplexer_4_out));  // open: sel, en
  Comparator #(.width(24)) comparator_1 (
    .a(register_file_1_data_a), .b(register_file_1_data_b), .eq(comparator_1_eq));  // open: gt, lt
  // Probe on nothing
  Multiplexer #(.select(2), .width(24)) multiplexer_5 (
    .in0(register_file_1_data_a), .in1(alu_1_p5), .in2(multiplexer_9_out), .in3(register_2_q),
    .out(multiplexer_5_out), .sel(forwarding_logic_1_sa));  // open: en
  Multiplexer #(.select(2), .width(24)) multiplexer_6 (
    .in0(register_file_1_data_b), .in1(alu_1_p5), .in2(multiplexer_9_out), .in3(register_2_q),
    .out(multiplexer_6_out), .sel(forwarding_logic_1_sb));  // open: en
  Multiplexer #(.width(10)) multiplexer_7 (
    .in0({main_1_p7[0], main_1_p9[8], main_1_p7[5], main_1_p7[2], main_1_p7[4:3], main_1_p7[1], main_1_p8}),
    .in1({10{1'b0}}), .out(multiplexer_7_out), .sel(or_2_out));  // open: en
  Register #(.width(24)) Jump (.D(adder_2_out), .en(1'b1), .Q(Jump_q), .clk(clock_1_out), .clr(1'b0));
  Register #(.width(24)) BTA (.D(adder_3_out), .en(1'b1), .Q(BTA_q), .clk(clock_1_out), .clr(1'b0));
  Register #(.width(24)) Immediate (.D(multiplexer_4_out), .en(1'b1), .Q(Immediate_q), .clk(clock_1_out), .clr(1'b0));
  Register #(.width(24)) DataA (.D(multiplexer_5_out), .en(1'b1), .Q(DataA_q), .clk(clock_1_out), .clr(1'b0));
  Register #(.width(24)) DataB (.D(multiplexer_6_out), .en(1'b1), .Q(DataB_q), .clk(clock_1_out), .clr(1'b0));
  Register #(.width(3)) Rd2 (.D(multiplexer_3_out), .en(1'b1), .Q(Rd2_q), .clk(clock_1_out), .clr(1'b0));
  Register #(.width(10)) EX (.D(multiplexer_7_out), .en(1'b1), .Q(EX_q), .clk(clock_1_out), .clr(1'b0));
  Multiplexer #(.width(24)) multiplexer_8 (
    .in0(DataB_q), .in1(Immediate_q), .out(multiplexer_8_out), .sel(EX_q[3]));  // open: en
  Register #(.width(1)) Zero (.D(alu_1_p3), .en(EX_q[8]), .Q(main_1_p2), .clk(clock_1_out), .clr(1'b0));
  // ALU alu_1: pin names not known; wires that end beside it: DataA_q, multiplexer_8_out, alu_1_p3, EX_q[2:0], alu_1_p5
  Register #(.width(4)) MEM (.D(EX_q[7:4]), .en(1'b1), .Q(MEM_q), .clk(clock_1_out), .clr(1'b0));
  Register #(.width(24)) Alu_Res (.D(alu_1_p5), .en(1'b1), .Q(Alu_Res_q), .clk(clock_1_out), .clr(1'b0));
  Register #(.width(24)) RB (.D(DataA_q), .en(1'b1), .Q(RB_q), .clk(clock_1_out), .clr(1'b0));
  Register #(.width(3)) Rd3 (.D(Rd2_q), .en(1'b1), .Q(Rd3_q), .clk(clock_1_out), .clr(1'b0));
  RAM #(.addrWidth(24), .dataWidth(24), .bus("separate")) ram_1 (
    .addr(Alu_Res_q), .din(RB_q), .data(ram_1_data), .str(MEM_q[0]), .sel(1'b1), .clk(clock_1_out),
    .ld(MEM_q[1]));  // open: clr
  Register #(.width(3)) Rd4 (.D(Rd3_q), .en(1'b1), .Q(Rd4_q), .clk(clock_1_out), .clr(1'b0));
  Register #(.width(1)) WB (.D(MEM_q[3]), .en(1'b1), .Q(WB_q), .clk(clock_1_out), .clr(1'b0));
  Multiplexer #(.width(24)) multiplexer_9 (
    .in0(Alu_Res_q), .in1(ram_1_data), .out(multiplexer_9_out), .sel(MEM_q[2]));  // open: en
  Register #(.width(24)) register_2 (.D(multiplexer_9_out), .en(1'b1), .Q(register_2_q), .clk(clock_1_out), .clr(1'b0));

  // Notes on the sheet:
  //   0 for normal
  //   1 1 for inst13 JAL
  //   2 for inst 6 JR 
  //   3 for inst 11 BEQ
  //   make sure OP table is correct
  //   Fix ALU
  //   signal Alu Src make sure to be imeediate when instruction is I type or J type
  //   signal for RGDst, chec much
  //   use EQ produced after reg file for PC control
  //   MUX for immediate source for Jar instruction
  //   Instruction Splitter: inst 23 -0
  //   if istruction is Rtyper then
  //   contents of rom_1 (hex, n*v repeats v):
  //   10c020 1fffe 111111
  //   23-22 is cond
  //   21-17 is Op
  //   16 is SF
  //   15-13 is Rd
  //   12-10 is Rt
  //   9-7Rs
  //   Stall
  //   Rd
  //   Rt
  //   Rs
  //   Rs
  //   Rs
  //   if JAL then 1
  //   if LUI then 2
  //   O.W zero
  //   opcode = jar
  //   use in PC Control
  //   0-2 is Alu OP (0 is lsb)
  //   3 is Alu Src
  //   4 is memWr
  //   5 is memRd
  //   6 is WBdata
  //   7 is RegWr
  //   8 is Z enable
  //   9 is Beq
  //   not R-type
endmodule

module Register_File (
  input  [2:0] RW,
  input  CLK,
  input  RegRW,
  input  [2:0] RA,
  input  [2:0] RB,
  input  [23:0] BusWR,
  output [23:0] R0,
  output [23:0] R1,
  output [23:0] Data_A,
  output [23:0] R2,
  output [23:0] Data_B,
  output [23:0] R3,
  output [23:0] R4,
  output [23:0] R5,
  output [23:0] R6,
  output [23:0] R7
);

  wire decoder_1_out0, decoder_1_out1, decoder_1_out2, decoder_1_out3, decoder_1_out4, decoder_1_out5,
       decoder_1_out6, decoder_1_out7, M0_2_out, M0_3_out, M0_4_out, M0_5_out, M0_6_out, M0_7_out, M0_8_out,
       M0_out;

  Decoder #(.select(3)) decoder_1 (
    .out0(decoder_1_out0), .out1(decoder_1_out1), .out2(decoder_1_out2), .out3(decoder_1_out3),
    .out4(decoder_1_out4), .out5(decoder_1_out5), .out6(decoder_1_out6), .out7(decoder_1_out7), .sel(RW));  // open: en
  and M0 (M0_out, decoder_1_out0, RegRW);
  and M0_2 (M0_2_out, decoder_1_out1, RegRW);
  and M0_3 (M0_3_out, decoder_1_out2, RegRW);
  and M0_4 (M0_4_out, decoder_1_out3, RegRW);
  and M0_5 (M0_5_out, decoder_1_out4, RegRW);
  and M0_6 (M0_6_out, decoder_1_out5, RegRW);
  and M0_7 (M0_7_out, decoder_1_out6, RegRW);
  and M0_8 (M0_8_out, decoder_1_out7, RegRW);
  Register #(.width(24)) u_R0 (.D(BusWR), .en(M0_out), .Q(R0), .clk(CLK), .clr(1'b1));
  Register #(.width(24)) u_R1 (.D(BusWR), .en(M0_2_out), .Q(R1), .clk(CLK));  // open: clr
  Register #(.width(24)) u_R2 (.D(BusWR), .en(M0_3_out), .Q(R2), .clk(CLK));  // open: clr
  Register #(.width(24)) u_R3 (.D(BusWR), .en(M0_4_out), .Q(R3), .clk(CLK));  // open: clr
  Register #(.width(24)) u_R4 (.D(BusWR), .en(M0_5_out), .Q(R4), .clk(CLK));  // open: clr
  Register #(.width(24)) u_R5 (.D(BusWR), .en(M0_6_out), .Q(R5), .clk(CLK));  // open: clr
  Register #(.width(24)) u_R6 (.D(BusWR), .en(M0_7_out), .Q(R6), .clk(CLK));  // open: clr
  Register #(.width(24)) u_R7 (.D(BusWR), .en(M0_8_out), .Q(R7), .clk(CLK));  // open: clr
  Multiplexer #(.select(3), .width(24)) multiplexer_1 (
    .in0(R0), .in1(R1), .in2(R2), .in3(R3), .in4(R4), .in5(R5), .in6(R6), .in7(R7), .out(Data_A), .sel(RA));  // open: en
  Multiplexer #(.select(3), .width(24)) multiplexer_2 (
    .in0(R0), .in1(R1), .in2(R2), .in3(R3), .in4(R4), .in5(R5), .in6(R6), .in7(R7), .out(Data_B), .sel(RB));  // open: en
endmodule
